# Fritzing sketch Pengendalian Micro Servo Menggunakan Bluetooth (saved by Fritzing 0.8.7b)

parts:
  Part1 = Bluetooth HC-05
  SERVO3 = Tower Pro SG90 servo [part_number=101246]
  Part2 = Arduino Uno (Rev3)

nets:
  N1: Part1.RXD, Part2.D11_PWM/MOSI
  N2: Part1.TXD, Part2.D10_PWM/SS
  GND: Part1.GND, SERVO3.GND, Part2.GND
  VCC: Part1.VCC, Part1.WAKEUP, Part2.5V
  N3: SERVO3.Signal, Part2.D9_PWM
  +5V: SERVO3.+5V, Part2.3V3

custom parts:
  Tower Pro SG90 servo: Original file by John De Cristofaro http://www.adafruit.com/products/1449 Adafruit Feedback Servo (Small) Edited by: e-radionica.com 28/9/2015
